// Logisim project CPU_simulation_starter_2024.circ as structural Verilog: 4 circuits, main circuit CPU_main
module CPU_main (
);

  wire alu_1_acc_ne_zero, and_1_out, and_2_out, clock_1_out, instruction_decoding_unit_1_bnez,
       instruction_decoding_unit_1_output_char, instruction_decoding_unit_1_stop,
       instruction_decoding_unit_1_use_memory, instruction_decoding_unit_1_write_acc,
       instruction_decoding_unit_1_write_memory, not_1_out;
  wire [3:0] instruction_decoding_unit_1_alu_operation;
  wire [6:0] bit_extender_1_out;
  wire [7:0] ACC_q, adder_1_out, alu_1_alu_to_acc, instruction_decoding_unit_1_addr_or_imm,
       multiplexer_1_out, multiplexer_2_out, PC_q, ValueSet_dout;
  wire [15:0] InstructionSet_data;

  not not_1 (not_1_out, instruction_decoding_unit_1_stop);
  Clock clock_1 (.out(clock_1_out));
  Adder adder_1 (.a(PC_q), .b(8'h1), .out(adder_1_out));  // open: cin, cout
  Register PC (.D(multiplexer_1_out), .clk(and_1_out), .Q(PC_q));  // open: en, clr
  Multiplexer #(.width(8)) multiplexer_1 (
    .in0(adder_1_out), .in1(multiplexer_2_out), .out(multiplexer_1_out), .sel(and_2_out));
  and and_1 (and_1_out, not_1_out, clock_1_out);
  ROM #(.dataWidth(16)) InstructionSet (.addr(PC_q), .data(InstructionSet_data));
  Instruction_Decoding_Unit instruction_decoding_unit_1 (
    .Instruction(InstructionSet_data), .ALU_Operation(instruction_decoding_unit_1_alu_operation),
    .Write_ACC(instruction_decoding_unit_1_write_acc), .Use_Memory(instruction_decoding_unit_1_use_memory),
    .Write_Memory(instruction_decoding_unit_1_write_memory), .BNEZ(instruction_decoding_unit_1_bnez),
    .Output_Char(instruction_decoding_unit_1_output_char), .Stop(instruction_decoding_unit_1_stop),
    .Addr_or_Imm(instruction_decoding_unit_1_addr_or_imm));
  RAM #(.asyncread("true"), .clearpin("true")) ValueSet (
    .addr(instruction_decoding_unit_1_addr_or_imm), .we(instruction_decoding_unit_1_write_memory),
    .clk(and_1_out), .din(ACC_q), .dout(ValueSet_dout));  // open: oe, clr
  and and_2 (and_2_out, instruction_decoding_unit_1_bnez, alu_1_acc_ne_zero);
  Register ACC (
    .D(alu_1_alu_to_acc), .en(instruction_decoding_unit_1_write_acc), .clk(and_1_out), .Q(ACC_q));  // open: clr
  Multiplexer #(.width(8)) multiplexer_2 (
    .in0(instruction_decoding_unit_1_addr_or_imm), .in1(ValueSet_dout), .out(multiplexer_2_out),
    .sel(instruction_decoding_unit_1_use_memory));
  Bit_Extender #(.out_width(7)) bit_extender_1 (.in(ACC_q), .out(bit_extender_1_out));
  TTY tty_1 (.data(bit_extender_1_out), .clk(and_1_out), .we(instruction_decoding_unit_1_output_char));  // open: clr
  ALU alu_1 (
    .ALU_Operation(instruction_decoding_unit_1_alu_operation), .From_ACC(ACC_q), .Input2(multiplexer_2_out),
    .ALU_to_ACC(alu_1_alu_to_acc), .ACC_NE_Zero(alu_1_acc_ne_zero));

  // Notes on the sheet:
  //   contents of InstructionSet (hex, n*v repeats v):
  //   102f 3000 1002 3001 2000 2501 400f 2000 3002 2001 3000 2002 3001 2010 3002 2600 3003 2602 3004 5000
  //   5001 f000
  //   Student id: 24804702
endmodule

module Instruction_Decoding_Unit (
  input  [15:0] Instruction,
  output [3:0] ALU_Operation,
  output Write_ACC,
  output Use_Memory,
  output Write_Memory,
  output BNEZ,
  output Output_Char,
  output Stop,
  output [7:0] Addr_or_Imm
);

  wire decoder_1_out1, decoder_1_out2;

  Decoder #(.select(4)) decoder_1 (
    .out1(decoder_1_out1), .out2(decoder_1_out2), .out3(Write_Memory), .out4(BNEZ), .out5(Output_Char),
    .out15(Stop), .sel(Instruction[15:12]));  // open: out0, out6, out7, out8, out9, out10, out11, out12, out13, out14, en
  or or_1 (Write_ACC, decoder_1_out1, decoder_1_out2);
  or or_2 (Use_Memory, decoder_1_out2, Write_Memory);

  assign Addr_or_Imm = Instruction[7:0];
  assign ALU_Operation = Instruction[11:8];
endmodule

module ALU (
  input  [3:0] ALU_Operation,
  input  [7:0] From_ACC,
  input  [7:0] Input2,
  output [7:0] ALU_to_ACC,
  output ACC_NE_Zero
);

  wire comparator_1_gt, comparator_1_lt, comparator_2_eq;
  wire [7:0] adder_1_out, and_1_out, ascii_to_hex_1_cout1, ascii_to_hex_1_cout2, bit_extender_1_out,
       shifter_1_out, xor_1_out;

  Adder adder_1 (.a(From_ACC), .b(Input2), .out(adder_1_out));  // open: cin, cout
  assign and_1_out = From_ACC & Input2;  // AND_Gate and_1, 8 bits wide
  Shifter #(.shift("lr")) shifter_1 (.in(From_ACC), .\dist (3'b100), .out(shifter_1_out));
  Comparator #(.mode("unsigned")) comparator_1 (
    .a(From_ACC), .b(Input2), .gt(comparator_1_gt), .lt(comparator_1_lt));  // open: eq
  Comparator comparator_2 (.a(From_ACC), .b({8{1'b0}}), .eq(comparator_2_eq));  // open: gt, lt
  assign xor_1_out = From_ACC ^ Input2;  // XOR_Gate xor_1, 8 bits wide
  assign bit_extender_1_out = {{7{1'b0}}, comparator_1_lt};  // Bit_Extender bit_extender_1
  not not_1 (ACC_NE_Zero, comparator_2_eq);
  ASCII_To_Hex ascii_to_hex_1 (.From_ACC(From_ACC), .cout1(ascii_to_hex_1_cout1), .cout2(ascii_to_hex_1_cout2));
  Multiplexer #(.select(4), .width(8)) multiplexer_1 (
    .in0(Input2), .in1(adder_1_out), .in2(and_1_out), .in3(xor_1_out), .in4(shifter_1_out),
    .in5(bit_extender_1_out), .in6(ascii_to_hex_1_cout2), .in7(ascii_to_hex_1_cout1), .out(ALU_to_ACC),
    .sel(ALU_Operation));  // open: in8, in9, in10, in11, in12, in13, in14, in15
endmodule

module ASCII_To_Hex (
  input  [7:0] From_ACC,
  output [7:0] cout1,
  output [7:0] cout2
);

  wire comparator_1_eq, comparator_1_lt, comparator_2_eq, comparator_2_lt, or_1_out, or_2_out;
  wire [7:0] adder_1_out, adder_2_out, adder_3_out, adder_4_out, bit_extender_1_out, bit_extender_2_out;

  // Probe on From_ACC[3:0]
  // Probe on From_ACC[7:4]
  assign bit_extender_1_out = {{4{1'b0}}, From_ACC[3:0]};  // Bit_Extender bit_extender_1
  assign bit_extender_2_out = {{4{1'b0}}, From_ACC[7:4]};  // Bit_Extender bit_extender_2
  Comparator comparator_1 (.a(bit_extender_1_out), .b(8'h9), .eq(comparator_1_eq), .lt(comparator_1_lt));  // open: gt
  Comparator comparator_2 (.a(bit_extender_2_out), .b(8'h9), .eq(comparator_2_eq), .lt(comparator_2_lt));  // open: gt
  or or_1 (or_1_out, comparator_1_eq, comparator_1_lt);
  or or_2 (or_2_out, comparator_2_eq, comparator_2_lt);
  Adder adder_1 (.a(bit_extender_1_out), .b(8'h57), .out(adder_1_out));  // open: cin, cout
  Adder adder_2 (.a(bit_extender_1_out), .b(8'h30), .out(adder_2_out));  // open: cin, cout
  Adder adder_3 (.a(8'h57), .b(bit_extender_2_out), .out(adder_3_out));  // open: cin, cout
  Adder adder_4 (.a(8'h30), .b(bit_extender_2_out), .out(adder_4_out));  // open: cin, cout
  Multiplexer #(.width(8)) multiplexer_1 (.in0(adder_1_out), .in1(adder_2_out), .out(cout1), .sel(or_1_out));
  Multiplexer #(.width(8)) multiplexer_2 (.in0(adder_3_out), .in1(adder_4_out), .out(cout2), .sel(or_2_out));
endmodule
