// Logisim project test.circ as structural Verilog: 1 circuit, main circuit main
module main (
  input  [7:0] C_in,
  input  [7:0] in_2,
  input  [7:0] in_3,
  input  [7:0] A,
  input  [7:0] B,
  input  [7:0] in_6,
  input  [7:0] in_7,
  output [7:0] C_out,
  output out_9,
  output out_10,
  output out_11,
  output [7:0] out_12,
  output [7:0] out_13
);

  wire and_1_out, comparator_2_eq, comparator_2_gt, comparator_2_lt, comparator_3_eq, comparator_3_gt,
       comparator_3_lt, or_1_out;

  Shifter #(.shift("lr")) shifter_1 (.in(C_in), .\dist (3'b100), .out(C_out));
  Comparator #(.mode("unsigned")) comparator_1 (.a(in_2), .b(in_3), .gt(out_9), .eq(out_10), .lt(out_11));
  Comparator #(.mode("unsigned")) comparator_2 (
    .a(A), .b(B), .gt(comparator_2_gt), .eq(comparator_2_eq), .lt(comparator_2_lt));
  Comparator #(.mode("unsigned")) comparator_3 (
    .a(in_6), .b(in_7), .gt(comparator_3_gt), .eq(comparator_3_eq), .lt(comparator_3_lt));
  and and_1 (and_1_out, comparator_2_gt, comparator_2_eq);
  // AND_Gate and_2 has open pins: in0=comparator_3_eq, in1=comparator_3_lt, out=open
  assign out_12 = {{7{1'b0}}, or_1_out};  // Bit_Extender bit_extender_1
  or or_1 (or_1_out, and_1_out, comparator_2_lt);
  assign out_13 = {{7{1'b0}}, comparator_3_gt};  // Bit_Extender bit_extender_2
endmodule
